# Fritzing sketch footMouse (saved by Fritzing 0.9.0b)

parts:
  Pro_Micro1 = Pro Micro
  Mouse = Thumb Joystick
  Wheel = Thumb Joystick
  Button_1 = Round Pushbutton
  Button_2 = Round Pushbutton

nets:
  N1: Pro_Micro1.GND#3, Button_1.leg1, Button_2.leg1
  N2: Pro_Micro1.D3, Button_2.leg0
  N3: Pro_Micro1.D4, Button_1.leg0
  N4: Pro_Micro1.D15/SCLK, Mouse.SEL
  N5: Pro_Micro1.D18/A0, Mouse.VERT
  N6: Pro_Micro1.D19/A1, Mouse.HORZ
  N7: Pro_Micro1.D20/A2, Wheel.VERT
  VCC: Pro_Micro1.VCC, Mouse.VCC, Wheel.VCC
  GND: Pro_Micro1.GND#23, Mouse.GND, Wheel.GND, Wheel.SEL

custom parts:
  Pro Micro: The SparkFun Pro Micro is a complete USB-based microcontoller development system, in a very small footprint, capable of implementing many types of projects. All programming can be done via the USB port.
